# Fritzing sketch recharge-arduino (saved by Fritzing 0.9.2b)
circuit board: 8.46667cm x 5.64444cm
breadboards: 1

parts:
  U1 = MCP73831 [package=THT]
  R1 = Resistor [tolerance=±5% resistance=470 package="0805 [SMD]"]
  R2 = Resistor [tolerance=±5% resistance=2.2k package="0805 [SMD]"]
  R3 = Resistor [tolerance=±5% resistance=470 package="0805 [SMD]"]
  C2 = Capacitor [package=1206]
  X1 = USB Connectors [package=usb-microb]
  CLED = smd LED [color="Red (633nm)" package="0603 [SMD]"]
  DLED = smd LED [color="Green (555nm)" package="0603 [SMD]"]
  10uF = Capacitor [package=1206]
  JP1 = Header 2 [package=jst-2-smd]
  IC1 = FT230XQ [package=qfn16-4x4]  # not connected
  XTAL3 = CRYSTAL - kHz [frequency="16 Mhz"]  # not connected
  IC2 = LM3480IM4 [package=sot23-3]  # not connected
  S1 = SWITCH-MOMENTARY-2 [package=tactile-switch-1101ne]  # not connected
  LED3 = smd LED [color="Green (570nm)" package="0603 [SMD]"]  # not connected
  LED2 = smd LED [color="Green (570nm)" package="0603 [SMD]"]  # not connected
  LED1 = smd LED [color="Green (570nm)" package="0603 [SMD]"]  # not connected
  J1 = male pin header, 18 pins [form="♂ (male)"]
  J2 = male pin header, 18 pins [form="♂ (male)"]
  U2 = ATMEGA32U4 [package=qfn]

nets:
  N1: U1.Pin_1, C2.2, JP1.1
  N2: U1.Pin_2, R2.Pin_0, R3.Pin_1, C2.1, X1.VBUS, 10uF.1, JP1.2
  N3: U1.Pin_3, CLED.cathode, DLED.anode
  N4: U1.Pin_4, R1.Pin_1, X1.GND, 10uF.2
  N5: U1.Pin_5, R2.Pin_1
  N6: R1.Pin_0, CLED.anode
  N7: R3.Pin_0, DLED.cathode
  N8: J1.pin1, U2.PE2_!HWB
  N9: J1.pin4, U2.PF7(ADC7)
  N10: J1.pin5, U2.PF6(ADC6)
  N11: J1.pin6, U2.PF5(ADC5)
  N12: J1.pin7, U2.PF4(ADC4)
  N13: J1.pin8, U2.PF1(ADC1)
  N14: J1.pin9, U2.PF0(ADC0)
  N15: J1.pin10, U2.AREF
  N16: J2.pin1, U2.PC7
  N17: J2.pin2, U2.PC6
  N18: J2.pin3, U2.PB6(ADC13)
  N19: J2.pin4, U2.PB5(ADC12)
  N20: J2.pin5, U2.PB4(ADC11)
  N21: J2.pin6, U2.PD7(ADC10)
  N22: J2.pin7, U2.PD6(ADC9)
  N23: J2.pin8, U2.PD4(ADC8)
  N24: J2.pin9, U2.AVCC
  N25: J2.pin10, U2.GND

custom parts:
  MCP73831: MCP73831 - Regulates battery changing
